# Fritzing sketch PushButtonRotaryEncoder (saved by Fritzing 0.9.3b)
breadboards: 1

parts:
  WeMos_D1_Mini1 = WeMos D1 Mini
  Rotary_Encoder = female pin header, 5 pins [form="♀ (female)"]
  R1 = Resistor [tolerance=±5% resistance=10k package=THT]

nets:
  3.3V: WeMos_D1_Mini1.3V3, Rotary_Encoder.pin2, R1.Pin_1
  SW: WeMos_D1_Mini1.D0, Rotary_Encoder.pin3, R1.Pin_0
  DT: WeMos_D1_Mini1.D5, Rotary_Encoder.pin4
  CLK: WeMos_D1_Mini1.D6, Rotary_Encoder.pin5
  GND: WeMos_D1_Mini1.G, Rotary_Encoder.pin1

notes:
  IoT, Push Button Rotary Encoder, 1.0.0
